# Fritzing sketch 푸쉬업 프리징 (saved by Fritzing 0.9.2b)
breadboards: 1

parts:
  부품1 = Arduino Uno (Rev3)
  LED1 = LED - 5mm [color="Red (633nm)" package="5 mm [THT]"]
  R1 = Resistor [tolerance=±5% resistance=220 package=THT]
  S1 = Pushbutton [package="[THT]"]
  부품2 = LCD1602-I2C
  BT1 = Bluetooth HC-06u [package=THT]

nets:
  GND: 부품1.GND, R1.Pin_1, S1.Pin_1, S1.Pin_2, 부품2.GND, BT1.GND
  5V: 부품1.5V, LED1.anode, 부품2.VCC, BT1.VCC
  N1: LED1.cathode, R1.Pin_0

custom parts:
  LCD1602-I2C: A standard character display, usually with 2x16 characters. Comes in many colors with LCM1602 IIC attached.
  Bluetooth HC-06u: Bluetooth HC-06 - face up, pins down 16.5mm x 37.5mm PCB
